// Digital circuit lab2_part2.dig as structural Verilog
module lab2_part2 (
  input  in0,
  input  in1,
  input  in2,
  input  in3,
  output seg_a,
  output seg_f,
  output seg_b,
  output seg_g,
  output seg_e,
  output seg_c,
  output seg_d,
  output seg_dp,
  output sign_a,
  output sign_f,
  output sign_b,
  output sign_g,
  output sign_e,
  output sign_c,
  output sign_d,
  output sign_dp
);

  wire and_1_out, and_2_out, and_3_out, and_4_out, and_5_out, and_6_out, and_7_out, and_8_out, not_1_out,
       not_2_out, not_3_out, not_4_out, undriven, undriven_2, undriven_3, xor_1_out, xor_3_out, xor_6_out,
       xor_9_out, xor_12_out;
  wire [2:0] xor_2_out;

  Seven_Seg seven_seg_1 (
    .a(sign_a), .b(sign_b), .c(sign_c), .d(sign_d), .e(sign_e), .f(sign_f), .g(sign_g), .dp(sign_dp));
  Seven_Seg seven_seg_2 (.a(seg_a), .b(seg_a), .c(seg_a), .d(seg_a), .e(seg_a), .f(seg_a), .g(seg_a), .dp(seg_a));
  not not_1 (not_1_out, in0);
  xor xor_1 (xor_1_out, not_1_out, 1'b1);
  xor xor_2 (xor_2_out[0], 1'b0, xor_1_out);
  and and_1 (and_1_out, 1'b1, not_1_out);
  and and_2 (and_2_out, xor_1_out, 1'b0);
  xor xor_3 (xor_3_out, and_1_out, and_2_out);
  not not_2 (not_2_out, in1);
  xor xor_4 (xor_3_out, not_2_out, 1'b0);
  and and_3 (and_3_out, 1'b0, not_2_out);
  and and_4 (and_4_out, xor_3_out, undriven);
  xor xor_5 (xor_2_out[1], undriven, xor_3_out);
  xor xor_6 (xor_6_out, and_3_out, and_4_out);
  Decoder #(.Selector_Bits(3)) decoder_1 (
    .sel(xor_2_out), .out_0(seg_a), .out_1(seg_a), .out_2(seg_a), .out_3(seg_a), .out_4(seg_a),
    .out_5(seg_a), .out_6(seg_a), .out_7(seg_a));
  not not_3 (not_3_out, in2);
  xor xor_7 (xor_6_out, not_3_out, 1'b0);
  xor xor_8 (xor_2_out[2], undriven_2, xor_6_out);
  and and_5 (and_5_out, 1'b0, not_3_out);
  and and_6 (and_6_out, xor_6_out, undriven_2);
  xor xor_9 (xor_9_out, and_5_out, and_6_out);
  not not_4 (not_4_out, in3);
  xor xor_10 (xor_9_out, not_4_out, 1'b0);
  and and_7 (and_7_out, 1'b0, not_4_out);
  and and_8 (and_8_out, xor_9_out, undriven_3);
  xor xor_11 (sign_g, undriven_3, xor_9_out);
  xor xor_12 (xor_12_out, and_7_out, and_8_out);

  assign seg_b = seg_a;
  assign seg_c = seg_a;
  assign seg_d = seg_a;
  assign seg_dp = seg_a;
  assign seg_e = seg_a;
  assign seg_f = seg_a;
  assign seg_g = seg_a;
  // also tied to GND on the sheet: xor_12_out

  // Notes on the sheet:
  //   Interface (do not edit the content inside this box)
  //   Outputs:
  //   Inputs
  //   Sign
  //   Decimal Number
endmodule

/* Test case:
in3 in2 in1 in0  sign_a sign_b sign_c sign_d sign_e sign_f sign_g  seg_a seg_b seg_c seg_d seg_e seg_f seg_g
 0   0   0   0    0      0      0      0      0      0      0       1     1     1     1     1     1     0
*/
